# Fritzing sketch Drawdio Breadboard Circuit Source (saved by Fritzing 0.7.12b)
breadboards: 1

parts:
  C3 = Ceramic Capacitor [capacitance=0.1µF package="100 mil [THT, multilayer]"]
  C5 = Ceramic Capacitor [capacitance=680pF package="100 mil [THT, multilayer]"]
  Q1 = PNP-Transistor [package="TO92 [THT]"]
  J1 = Piezo Speaker
  R1 = Resistor [tolerance=±5% resistance=10M package=THT]
  R2 = Resistor [tolerance=±5% resistance=10 package=THT]
  R3 = Resistor [tolerance=±5% resistance=10k package=THT]
  R4 = Resistor [tolerance=±5% resistance=300k package=THT]
  C4 = Electrolytic Capacitor [capacitance=100µF package="100 mil [THT, electrolytic]"]
  U1 = 555 Timer [package="DIP8 [THT]"]
  VCC1 = Battery

nets:
  N1: C3.0, U1.Control_Voltage
  N2: C3.1, C5.0, J1.pin1, R1.Pin_0, R2.Pin_1, U1.Ground, VCC1.-
  N3: C5.1, R1.Pin_1, R4.Pin_1, U1.Trigger, U1.Threshold
  N4: Q1.E, R3.Pin_1, U1.Reset, U1.Vcc_Supply_Voltage, VCC1.+
  N5: Q1.B, U1.Output
  N6: Q1.C, R2.Pin_0, C4.-
  N7: J1.pin2, C4.+
  N8: R3.Pin_0, U1.Discharge

notes:
  Human
