# Fritzing sketch Drawdio Veroboard Circuit Source (saved by Fritzing 0.7.12b)
breadboards: 1
perfboards: 1

parts:
  C5 = Ceramic Capacitor [capacitance=680pF package="100 mil [THT, multilayer]"]
  J1 = Piezo Speaker
  R1 = Resistor [tolerance=±5% resistance=10M package=THT]
  R3 = Resistor [tolerance=±5% resistance=10k package=THT]
  R4 = Resistor [tolerance=±5% resistance=300k package=THT]
  U1 = 555 Timer [package="DIP8 [THT]"]
  VCC1 = Battery
  C6 = Electrolytic Capacitor [capacitance=100µF package="100 mil [THT, electrolytic]"]
  C3 = Ceramic Capacitor [capacitance=0.1µF package="0603 [SMD, multilayer]"]
  U2 = 555 Timer [package="DIP8 [THT]"]  # not connected
  J2 = Piezo Speaker  # not connected
  C7 = Electrolytic Capacitor [capacitance=100µF package="100 mil [THT, electrolytic]"]  # not connected
  C8 = Ceramic Capacitor [capacitance=0.1µF package="0603 [SMD, multilayer]"]  # not connected
  VCC2 = Battery  # not connected
  R5 = Resistor [tolerance=±5% resistance=300k package=THT]  # not connected
  R6 = Resistor [tolerance=±5% resistance=10k package=THT]  # not connected
  R7 = Resistor [tolerance=±5% resistance=10M package=THT]  # not connected
  C10 = Ceramic Capacitor [capacitance=680pF package="100 mil [THT, multilayer]"]  # not connected

nets:
  N1: C5.0, J1.pin1, R1.Pin_0, U1.Ground, VCC1.-, C3.1
  N2: C5.1, R1.Pin_1, R4.Pin_1, U1.Trigger, U1.Threshold
  N3: J1.pin2, C6.-
  N4: R3.Pin_0, U1.Discharge
  N5: R3.Pin_1, U1.Reset, U1.Vcc_Supply_Voltage, VCC1.+
  N6: U1.Output, C6.+
  N7: U1.Control_Voltage, C3.0

notes:
  Human
  Pencil Lead
  Hand
